# Fritzing sketch esquema (saved by Fritzing 0.9.3b)

parts:
  KY-4 = Keyes Relay [package=THT]
  Raspberry_Pi_1 = Raspberry Pi 3 [part_number=RPI-3-V1.2]

nets:
  N1: KY-4.signal, Raspberry_Pi_1.GPIO18
  N2: KY-4.power, Raspberry_Pi_1.5V
  N3: KY-4.ground, Raspberry_Pi_1.GND

notes:
  Lamp
  220V GND
  220V

custom parts:
  Keyes Relay: The Keyes 5V relay module is suitable for SCM development, home appliance control. It uses a 5V~12V TIL control signal which can control DC / AC signal.
